// Digital circuit RV5-PROCESSOR.dig as structural Verilog
module RV5_PROCESSOR (
  input  clock
);

  wire a_eq_b, a_lt_b, alu_bsel, alu_op, br_jmp, branch_sel, carry, dm_mem_wen, haltreq, jal_sel, jalr_sel,
       jump_progbuf, ld_signext, mem_b, mem_h, memren, memwen, memwen_t, regwen, regwen_t, resumereq;
  wire [1:0] alu_asel, wb_sel;
  wire [2:0] funct3, rv5_control_logic_1_p4;
  wire [4:0] rd_t, rs1_t;
  wire [11:0] funct12;
  wire [19:0] inst;
  wire [31:0] alu_out, dm_mem_addr, dm_mem_rdata, dm_mem_wdata, imm_signext, multiplexer_1_out,
       multiplexer_2_out, npc, npc_t, pc, R_rs1, R_rs2, rv5_memory_1_out, wb, wb_t;
  wire [31:2] add_1_s;

  // RV5_PCU rv5_pcu_1: pin names not known; wires that end beside it: imm_signext, alu_out, jalr_sel, br_jmp, clock, npc_t, pc, npc
  RV5_DEBUG_SYSTEM rv5_debug_system_1 (
    .clk(clock), .dm_mem_rdata(dm_mem_rdata), .R_rs1(R_rs1), .regwen(regwen), .memwen(memwen),
    .rd(inst[11:7]), .rs1(inst[19:15]), .wb(wb), .pc(pc), .npc(npc), .opcode(inst[6:0]), .funct3(funct3),
    .funct12(funct12), .haltreq(haltreq), .resumereq(resumereq), .jump_progbuf(jump_progbuf),
    .dm_mem_wdata(dm_mem_wdata), .dm_mem_wen(dm_mem_wen), .dm_mem_addr(dm_mem_addr), .regwen_2(regwen_t),
    .memwen_2(memwen_t), .rd_2(rd_t), .rs1_2(rs1_t), .wb_2(wb_t), .npc_2(npc_t));
  // RV5_CONTROL_LOGIC rv5_control_logic_1: pin names not known; wires that end beside it: inst[6:0], funct3, funct12, rv5_control_logic_1_p4, regwen, memwen, memren, mem_b, mem_h, ld_signext, alu_asel, alu_bsel, alu_op, branch_sel, jal_sel, jalr_sel, wb_sel
  RV5_IMM_GEN rv5_imm_gen_1 (
    .INSTR_32({funct12, inst[19:15], funct3, inst[11:0]}), .imm_sel(rv5_control_logic_1_p4), .imm(imm_signext));
  RV5_GPR rv5_gpr_1 (
    .RS1(rs1_t), .RS2(funct12[4:0]), .D_in(wb_t), .clk(clock), .RD(rd_t), .WEN(regwen_t), .RA(R_rs1),
    .RB(R_rs2));  // open: RD0
  Multiplexer #(.Bits(32)) multiplexer_1 (.sel(alu_bsel), .in_0(R_rs2), .in_1(imm_signext), .out(multiplexer_1_out));
  Multiplexer #(.Selector_Bits(2), .Bits(32)) multiplexer_2 (
    .sel(alu_asel), .in_0(R_rs1), .in_1(pc), .in_2({32{1'b0}}), .in_3({32{1'b0}}), .out(multiplexer_2_out));
  // RV5_ALU rv5_alu_1: pin names not known; wires that end beside it: multiplexer_2_out, alu_op, multiplexer_1_out, alu_out, carry, a_eq_b, a_lt_b
  RV5_BRANCH_COND_GEN rv5_branch_cond_gen_1 (
    .branch_sel(branch_sel), .jal_sel(jal_sel), .funct3(funct3), .eq(a_eq_b), .slt(a_lt_b), .carry(carry),
    .br_jmp(br_jmp));
  RV5_MEMORY rv5_memory_1 (
    .addr(alu_out), .wdata(R_rs2), .wen(memwen_t), .ren(memren), .clk(clock), .\byte (mem_b), .half(mem_h),
    .signext(ld_signext), .addr_inst(pc), .addr_dm(dm_mem_addr), .wen_dm(dm_mem_wen),
    .wdata_dm(dm_mem_wdata), .out(rv5_memory_1_out), .out_inst({funct12, inst[19:15], funct3, inst[11:0]}),
    .out_dm(dm_mem_rdata));
  Add #(.Bits(30)) add_1 (.a(pc[31:2]), .b({30{1'b0}}), .c_i(1'b1), .s(add_1_s));  // open: c_o
  Multiplexer #(.Selector_Bits(2), .Bits(32)) multiplexer_3 (
    .sel(wb_sel), .in_0(alu_out), .in_1({add_1_s, 2'b00}), .in_2(rv5_memory_1_out), .in_3({32{1'b0}}),
    .out(wb));

  // Other names for the same wires on the sheet: clk = clock; opcode[6:0] = inst[6:0]; rd[4:0] = inst[11:7];
  //   inst (some bits) = {funct12, funct3}; rs1[4:0] = inst[19:15]; rs2[4:0] = funct12[4:0]

  // Notes on the sheet:
  //   clock: Hz: 5000
  //   TODO: scrap pipeline stage division
  //   R_rs1 - done
  //   R_rs2 - done
  //   op1 op2 - done
  //   tri-state for one-hot mux
  //   PCU simplify - branch condition in control logic - done
  //   alu_asel = 2 -> Can go into register via r0? - No, we would need a mux to select rs1
  //   Startup script
  //   Think about memory
  //   Debug sep - done
  //   Note: In the debug module I have
  //   something set up to override
  //   this clock to maximum when debug
  //   work needs to be done.
  //   It's definitely a hack but worth it
  //   for the debugging performance.
  //   TLDR: The clock speed that you set 
  //   here really just dictates how 
  //   fast it will go *most* of the time.
  //   (Unless you disable that feature.)
  //   RISC-V CPU:
  //   Instruction memory
  //   In a Harvard-style CPU, there would
  //   be actual instruction memory here.
  //   Instead, we have a tunnel to our
  //   memory block and a tunnel back.
  //   This is a good compromise for us.
  //   However, another option is doing
  //   a fetch/execute design, where
  //   we spend a clock cycle getting the
  //   instruction and then another using it.
  //   (Or, of course, we could pipeline
  //   this processor.)
  //   About the CPU
  //   This is a single-cycle RV32I processor. In addition to the base instruction set, it also implements
  //   the Ziscr extension and contains a debug module.
  //   Although it is single-cycle, it is organized according to pipeline stages. 
  //   Tunnels that cross stages are aliased as prefixed with their destination stage; for example, alu-out
  //   becomes IF-alu-out when crossing into the IF stage. Because this CPU is single-cycle, these tunnels
  //   are equivilent, and at this point it is simply an organizational tool.
  //   Additionally, this is a Von Neumann architecture, and so instruction memory and data memory are
  //   merged. This makes it look slightly different than some educational datapath diagrams you might
  //   see, which sometimes show the Harvard style.
  //   RALU
endmodule
